// Logisim project Decoder_8_bits_to_7_segment.circ as structural Verilog: 1 circuit, main circuit main
module main (
  input  I0,
  input  I1,
  input  I2,
  input  I3,
  input  I4,
  input  I5,
  input  I6,
  input  I7,
  output g3,
  output f3,
  output e3,
  output d3,
  output c3,
  output b3,
  output a3,
  output g2,
  output f2,
  output e2,
  output d2,
  output c2,
  output b2,
  output a2,
  output g1,
  output f1,
  output e1,
  output d1,
  output c1,
  output b1,
  output a1
);

  ROM #(.dataWidth(21)) rom_1 (
    .addr({I7, I6, I5, I4, I3, I2, I1, I0}),
    .data({g3, f3, e3, d3, c3, b3, a3, g2, f2, e2, d2, c2, b2, a2, g1, f1, e1, d1, c1, b1, a1}));
endmodule
